# Fritzing sketch masthesad Sketchfinal.v02.01 (saved by Fritzing 0.9.3b)
circuit board: 5.81831cm x 5.66656cm
breadboards: 1

parts:
  Part1 = Arduino Nano (Rev3.0) (ICSP)
  Part2 = NRF24L01+ Breakout Board
  Q2 = Basic MosFET N-Channel [part_number=IRLB3034PdF package="TO220 [THT]"]
  Anchor = Screw terminal - 2 pins [package=THT]
  JP1 = #4 Stand Off [package=stand-off]  # not connected
  JP2 = #4 Stand Off [package=stand-off-tight]  # not connected
  JP3 = #4 Stand Off [package=stand-off-tight]  # not connected
  JP4 = #4 Stand Off [package=stand-off-tight]  # not connected
  12V = Screw terminal - 2 pins [package=THT]
  WSP = screw terminal, 3 pins
  WD = screw terminal, 3 pins
  J1 = female pin header, 15 pins [form="♀ (female)"]  # not connected
  J2 = female pin header, 15 pins [form="♀ (female)"]
  J3 = double row female pin header, 8 pins [form="♀ (female)"]  # not connected
  R1 = Resistor [tolerance=±5% resistance=10k package=THT]

nets:
  N1: Part1.D1/TX, J2.pin1
  GND: Part1.GND, Part2.GND, Q2.source, 12V.pin2, WSP.pin2, WD.pin2, R1.Pin_0
  N2: Part1.D7, Q2.gate
  N3: Part1.D9, Part2.CE
  N4: Part1.D10, Part2.CS, J2.pin13
  N5: Part1.D11/MOSI, Part2.MOSI
  N6: Part1.D12/MISO, Part2.MISO, J2.pin15
  N7: Part1.VIN, Anchor.pin1, 12V.pin1, WSP.pin1
  N8: Part1.A2, WSP.pin3
  N9: Part1.A1, WD.pin3
  3.3V: Part1.3V3, Part2.VCC
  N10: Part1.D13/SCK, Part2.SCK

custom parts:
  Basic MosFET N-Channel: A MOSFET N-Channel Transistor
  #4 Stand Off: #4 Stand Off This is the mechanical footprint for a #4 phillips button head screw. Use the keepout ring to avoid running the screw head into surrounding components. SKU : PRT-00447
  #4 Stand Off: #4 Stand Off This is the mechanical footprint for a #4 phillips button head screw. Use the keepout ring to avoid running the screw head into surrounding components. SKU : PRT-00447

// code stored in the sketch: sendrecive.ino
#include<SPI.h>
#include<RF24.h>
#include<stdlib.h>
//Setup Variables
int LastValue;
#define Offset 0;
int anchor = 7;
int WSsensorPin = 1;
int WDsensorPin = 2;
// ce, csn pins
RF24 radio(10, 9) ;

void setup(void) {
  while (!Serial) ;
  LastValue = 1;
  Serial.begin(9600) ;
  pinMode(anchor, INPUT);
  radio.begin() ;
  radio.setPALevel(RF24_PA_MAX) ;
  radio.setChannel(0x76) ;
  radio.openWritingPipe(0xF0F0F0F0E1LL) ;
  const uint64_t pipe = 0xE8E8F0F0E1LL ;
  radio.openReadingPipe(1, pipe) ;
  radio.enableDynamicPayloads() ;
  radio.powerUp() ;
  
}

void loop(void) {
  radio.startListening() ;
  Serial.println("Starting loop. Radio on.") ;
  char receivedMessage[4] = {0} ;
  Serial.println(receivedMessage);
  if (radio.available()) {
    radio.read(receivedMessage, sizeof(receivedMessage));
    Serial.println(receivedMessage) ;
    Serial.println("Turning off the radio.") ;
    radio.stopListening() ;
    String stringMessage(receivedMessage) ;
    Serial.println(stringMessage);

    if (stringMessage == "G1") {
      Serial.println("Looks like they want a string!") ;
      String datastring = "xxxxxxxx";
      const char data[10] = "xxxxxxxx";
      const char text[2][5] = {
        "99.9",
        "180"
      };
      int windDirection;
      float wndSpeed;
      windDirection = getvanedir();
      wndSpeed = getwindSpeed();

       //digitalWrite(anchor, LOW);

      //Print voltage and windspeed to serial
      Serial.print("Wind speed: ");
      Serial.println(wndSpeed);
      Serial.print("Wind dir: ");
      Serial.println(windDirection);
      Serial.print("\t");
      dtostrf(wndSpeed, 5, 1, text[0]);
      dtostrf(windDirection, 3, 0, text[1]);
      datastring = text[0];
      datastring += ",";
      datastring += text[1];
//      text += String(windDirection);
      //Serial.println(text);
      //delay(sensorDelay);
      digitalWrite(anchor, HIGH);
      radio.write(text, sizeof(text)) ;
      Serial.println("We sent our message.") ;
    }
    else if (stringMessage == "G0") {
      Serial.println("Looks like they want a string!") ;
      Serial.println(stringMessage) ;
      char text[] = "xxxx" ;
      int windDirection;
      float wndSpeed;
      windDirection = getvanedir();
      wndSpeed = getwindSpeed();

      //Print voltage and windspeed to serial
      Serial.print("Wind speed: ");
      Serial.println(wndSpeed);
      Serial.print("\t");
      Serial.print("Wind dir: ");
      Serial.println(windDirection);
      Serial.print("\t");
      dtostrf(wndSpeed, 5, 1, text);
      //text += String(windDirection);
      //delay(sensorDelay);
      digitalWrite(anchor, LOW);
      Serial.println(text);
      radio.write(text, sizeof(text)) ;
      Serial.println("We sent our message.") ;

    }
    else {
      Serial.println("unknown stringxxx!") ;
      Serial.println(stringMessage) ;
      //const char text[] = "xxxxx" ;
      //      float CalDirection;
      //      float windSpeed;
      //      CalDirection = getvanedir();
      //      windSpeed = getwindSpeed();

      //digitalWrite(anchor, LOW);
      //float tmp;
      //tmp = getwindSpeed();
      //Print voltage and windspeed to serial
      //      Serial.print("Wind speed: ");
      //      Serial.println(windSpeed);
      //      Serial.print("Wind dir: ");
      //      Serial.println(CalDirection);
      //      Serial.print("\t");
      //      dtostrf(windSpeed, 5, 1, text);
      //delay(sensorDelay);
      //     digitalWrite(anchor, HIGH);
      //      Serial.println(text);
      //      radio.write(text, sizeof(text)) ;
      //      Serial.println("We sent our message.") ;
    }
  }
//else {
//  Serial.println("radio Not Available.") ;
//  radio.printDetails();
//  radio.stopListening() ;
//}
  delay(200);

}



int getvanedir() {
  int result = 0;
  int VaneValue;// raw analog value from wind vane
  int Direction;// translated 0 - 360 direction
  int CalDirection;// converted value with offset applied
  VaneValue = analogRead(WDsensorPin);
  Direction = map(VaneValue, 0, 1023, 0, 360);
  CalDirection = Direction + Offset;

  if (CalDirection > 360)
    CalDirection = CalDirection - 360;
  if (CalDirection < 0)
    CalDirection = CalDirection + 360;

  // Only update the display if change greater than 2 degrees.
  if (abs(CalDirection - LastValue) > 5)
  {
  Serial.print(VaneValue); Serial.print("\t\t");
  Serial.print(CalDirection); Serial.print("\t\t");
  getHeading(CalDirection);
  LastValue = CalDirection;
  }
  result = CalDirection;
  return result;
}

float getwindSpeed() {
  float windSpeed = 0; // Wind speed in meters per second (m/s)
  float voltageMin = .4; // Mininum output voltage from anemometer in mV.
  float windSpeedMin = 0; // Wind speed in meters/sec corresponding to minimum voltage
  float voltageMax = 2.0; // Maximum output voltage from anemometer in mV.
  float windSpeedMax = 32; // Wind speed in meters/sec corresponding to maximum voltage
  float voltageConversionConstant = .004882814;
  float sensorVoltage;
  float sensorValue;
  float result = 0;
  sensorValue = analogRead(WSsensorPin);//Get a value between 0 and 1023 from the analog pin connected to the anemometer
  Serial.print("sensor Value ");
  Serial.println(sensorValue);
  sensorVoltage = sensorValue * voltageConversionConstant; //Convert sensor value to actual voltage
  Serial.print("sensor Voltage");
  Serial.println(sensorVoltage);
  //Convert voltage value to wind speed using range of max and min voltages and wind speed for the anemometer
  if (sensorVoltage <= voltageMin) {
    windSpeed = 0; //Check if voltage is below minimum value. If so, set wind speed to zero.
  } else {
    windSpeed = (sensorVoltage - voltageMin) * windSpeedMax / (voltageMax - voltageMin); //For voltages above minimum value, use the linear relationship to calculate wind speed.
  }
  result = windSpeed;
  return result;

}
// Converts compass direction to heading
void getHeading(int direction) {
  if (direction < 22)
    Serial.println("N");
  else if (direction < 67)
    Serial.println("NE");
  else if (direction < 112)
    Serial.println("E");
  else if (direction < 157)
    Serial.println("SE");
  else if (direction < 212)
    Serial.println("S");
  else if (direction < 247)
    Serial.println("SW");
  else if (direction < 292)
    Serial.println("W");
  else if (direction < 337)
    Serial.println("NW");
  else
    Serial.println("N");
}
